# Fritzing sketch pcb (saved by Fritzing 0.9.4)

parts:
  WeMos_D1_Mini1 = WeMos D1 Mini
  WeMos_D1_Mini_Relay_Shield_V1 = WeMos D1 Mini Relay Shield V2
  J3 = male pin header, 4 pins [form="♂ (male)"]
  Connettore_Scheda_Madre = male pin header, 5 pins [form="♂ (male)"]  # not connected
  Pulsante_Accensione_Case = Pushbutton [package=THT]

nets:
  5V: WeMos_D1_Mini1.5V, WeMos_D1_Mini_Relay_Shield_V1.5V
  N1: WeMos_D1_Mini1.D1, WeMos_D1_Mini_Relay_Shield_V1.D1
  N2: WeMos_D1_Mini1.G, WeMos_D1_Mini_Relay_Shield_V1.G
  N3: WeMos_D1_Mini_Relay_Shield_V1.COM, J3.pin4, Pulsante_Accensione_Case.leg0
  N4: WeMos_D1_Mini_Relay_Shield_V1.NO, J3.pin3, Pulsante_Accensione_Case.leg1
